# Fritzing sketch AutoAmp (saved by Fritzing 0.9.3b)
stripboards: 1

parts:
  R1 = Rotary Potentiometer (Large) [maximum_resistance=100kΩ package=THT]  # not connected
  R2 = Slide Potentiometer [maximum_resistance=10kΩ]
  J4 = male pin header, 2 pins [form="♂ (male)"]
  R3 = Slide Potentiometer [maximum_resistance=10kΩ]
  J6 = male pin header, 2 pins [form="♂ (male)"]
  R4 = Slide Potentiometer [maximum_resistance=10kΩ]
  J8 = male pin header, 2 pins [form="♂ (male)"]
  J9 = Basic Servo
  J10 = Basic Servo
  J11 = Basic Servo
  LED1 = LED - 5mm [color="Orange (620nm)" package="5 mm [THT]"]
  LED2 = LED - 5mm [color="Red (635nm)" package="5 mm [THT]"]
  LED3 = LED - 5mm [color="Blue (470nm)" package="5 mm [THT]"]
  J12 = female pin header, 3 pins [form="♀ (female)"]
  J13 = female pin header, 2 pins [form="♀ (female)"]  # not connected
  J14 = male pin header, 3 pins [form="♂ (male)"]
  J15 = female pin header, 2 pins [form="♀ (female)"]
  J16 = female pin header, 2 pins [form="♀ (female)"]
  J17 = female pin header, 2 pins [form="♀ (female)"]
  J18 = male pin header, 2 pins [form="♂ (male)"]
  R5 = Resistor [tolerance=±5% resistance=220 package=THT]
  Digital_Panel_Meter_Voltage_DMS-20PC_by_Murata1 = Digital Panel Meter, Voltage, DMS-20PC  # not connected
  7_Segment1 = 7 Segment Display  # not connected
  M1 = DC Motor
  IC1 = L293D [package=THT]
  Part2 = Arduino Mega 2560 (Rev3)
  IC2 = L293D [package=THT]

nets:
  N1: R2.wiper, J4.pin1
  N2: R3.wiper, J6.pin1
  N3: R4.wiper, J8.pin1
  GND: J9.gnd, J10.gnd, J11.gnd
  VCC: J9.vcc, J10.vcc, J11.vcc
  N4: LED1.cathode, LED2.cathode, LED3.cathode, R5.Pin_1
  N5: LED1.anode, J12.pin2
  N6: LED2.anode, J12.pin1
  N7: LED3.anode, J12.pin3
  N8: J14.pin1, Part2.D14/TX3
  N9: J14.pin2, Part2.D15/RX3
  N10: J14.pin3, Part2.D16_PWM/TX2
  N11: J15.pin1, Part2.D18/TX1
  N12: J15.pin2, Part2.A13
  N13: J16.pin1, Part2.D20/SDA
  N14: J16.pin2, Part2.A15
  N15: J17.pin1, Part2.D19/RX1
  N16: J17.pin2, Part2.A14
  N17: J18.pin1, Part2.5V
  N18: J18.pin2, Part2.GND
  N19: M1.pin_1, IC1.Out_2_(_Controlled_by_Enable_1_)
  N20: M1.pin_2, IC1.Out_1_(_Controlled_by_Enable_1_)
  N21: IC1.Enable_1, IC2.Enable_1
  GND_2: IC1.0V, IC2.0V
  N22: IC1.+Vmotor, IC2.+Vmotor
  N23: IC1.Enable_2, IC2.Enable_2
