# Fritzing sketch FootSwitch (saved by Fritzing 0.9.3b)
stripboards: 5
breadboards: 1

parts:
  Solo_LED = LED - 5mm [color="Red (633nm)" package="5 mm [THT]"]
  Solo_Switch = Toggle Switch [package=THT]
  Ch2_LED = LED - 5mm [color="Orange (620nm)" package="5 mm [THT]"]
  Ch1_LED = LED - 5mm [color="Blue (525nm)" package="5 mm [THT]"]
  Amp_Switch = SWITCH-DPDT [package=gpi-152-3013]
  Ethernet_Jack2 = female pin header, 8 pins [form="♀ (female)"]
  AMP_LED = RGB LED (com. cathode, rgb) [package="5 mm [THT]"]
  Ch3 = SWITCH-DPDT [package=gpi-152-3013]
  Ch2 = SWITCH-DPDT [package=gpi-152-3013]
  Ch1 = SWITCH-DPDT [package=gpi-152-3013]
  Reverb_Switch = Toggle Switch [package=THT]
  Solo_LED1 = LED - 5mm [color="Blue (505nm)" package="5 mm [THT]"]
  J1 = female pin header, 5 pins [form="♀ (female)"]
  J2 = female pin header, 2 pins [form="♀ (female)"]
  Ch3_LED = LED - 5mm [color="Red (633nm)" package="5 mm [THT]"]
  J3 = female pin header, 2 pins [form="♀ (female)"]
  J4 = female pin header, 2 pins [form="♀ (female)"]
  J5 = female pin header, 3 pins [form="♀ (female)"]
  J6 = female pin header, 3 pins [form="♀ (female)"]
  J7 = female pin header, 2 pins [form="♀ (female)"]
  J8 = female pin header, 2 pins [form="♀ (female)"]
  J9 = female pin header, 2 pins [form="♀ (female)"]
  J10 = female pin header, 2 pins [form="♀ (female)"]
  J11 = female pin header, 2 pins [form="♀ (female)"]
  J12 = female pin header, 2 pins [form="♀ (female)"]
  J13 = female pin header, 3 pins [form="♀ (female)"]
  R6 = Resistor [tolerance=±5% resistance=220 package=THT]
  R7 = Resistor [tolerance=±10% resistance=220 package=THT]
  R8 = Resistor [tolerance=±5% resistance=220 package=THT]
  J16 = female pin header, 3 pins [form="♀ (female)"]
  J17 = female pin header, 3 pins [form="♀ (female)"]
  J18 = female pin header, 3 pins [form="♀ (female)"]
  J15 = male pin header, 5 pins [form="♂ (male)"]
  D5 = Rectifier Diode [part_number=1N4001 package="300 mil [THT]"]
  Q5 = PNP-Transistor [package="TO92 [THT]"]
  R20 = Resistor [tolerance=±5% resistance=47k package=THT]
  R21 = Resistor [tolerance=±5% resistance=1k package=THT]
  R22 = Resistor [tolerance=±5% resistance=220 package=THT]
  R23 = Resistor [tolerance=±5% resistance=220 package=THT]
  Q6 = PNP-Transistor [package="TO92 [THT]"]
  R24 = Resistor [tolerance=±5% resistance=10k package=THT]
  R25 = Resistor [tolerance=±5% resistance=220 package=THT]
  R26 = Resistor [tolerance=±5% resistance=10k package=THT]
  Q7 = NPN-Transistor [package="TO92 [THT]"]
  U6 = TLP621 [package=THT]
  D6 = Rectifier Diode [part_number=1N4001 package="300 mil [THT]"]
  D3 = Rectifier Diode [part_number=1N4001 package="300 mil [THT]"]
  D4 = Rectifier Diode [part_number=1N4001 package="300 mil [THT]"]
  R19 = Resistor [tolerance=±5% resistance=220 package=THT]
  Ethernet_Jack = female pin header, 9 pins [form="♀ (female)"]
  R27 = Resistor [tolerance=±5% resistance=220 package=THT]
  U7 = 941H-2C-5D [package=relay-5v]
  U8 = 941H-2C-5D [package=relay-5v]
  R28 = Resistor [tolerance=±5% resistance=220 package=THT]  # not connected
  R29 = Resistor [tolerance=±5% resistance=220 package=THT]  # not connected
  R30 = Resistor [tolerance=±5% resistance=220 package=THT]  # not connected
  R31 = Resistor [tolerance=±5% resistance=220 package=THT]  # not connected
  R32 = Resistor [tolerance=±5% resistance=220 package=THT]  # not connected

nets:
  N1: Solo_LED.cathode, AMP_LED.common_cathode, Solo_LED1.cathode, J5.pin1, J6.pin1, J7.pin1, J8.pin1, J9.pin2
  N2: Solo_LED.anode, Solo_Switch.L2, J7.pin2
  N3: Solo_Switch.L1, J17.pin2, J18.pin2, Ethernet_Jack.pin4
  N4: Solo_Switch.COM, R6.Pin_0
  GND: Ch2_LED.cathode, Ch1_LED.cathode, Ch3_LED.cathode, J10.pin1, J11.pin1, J12.pin1, J13.pin1, J16.pin1, D5.cathode, R20.Pin_0, D4.anode, Ethernet_Jack.pin8, Ethernet_Jack.pin9
  N5: Ch2_LED.anode, J11.pin2, J13.pin3, J16.pin3
  N6: Ch1_LED.anode, Ch3_LED.anode, J10.pin2, J12.pin2, J13.pin2, J16.pin2
  N7: Amp_Switch.2, R8.Pin_0
  Variable Power: Amp_Switch.5, Ch3.3, Ch2.3, Ch2.6, Ch1.3, J9.pin1, R6.Pin_1, R7.Pin_1, R8.Pin_1, Ethernet_Jack.pin1, R27.Pin_0
  N8: Amp_Switch.1, AMP_LED.red_anode, AMP_LED.green_anode, J5.pin2, J6.pin2
  N9: Amp_Switch.3, AMP_LED.blue_anode, J5.pin3, J6.pin3
  N10: Amp_Switch.6, J17.pin1, J18.pin1, Ethernet_Jack.pin3
  N11: Ethernet_Jack2.pin1, J15.pin3
  N12: Ethernet_Jack2.pin2, U8.13
  N13: Ethernet_Jack2.pin3, J1.pin1
  N14: Ethernet_Jack2.pin4, J1.pin2
  N15: Ethernet_Jack2.pin5, J1.pin3
  N16: Ethernet_Jack2.pin6, J1.pin4
  N17: Ethernet_Jack2.pin7, J1.pin5
  N18: Ethernet_Jack2.pin8, J15.pin1, U7.1, U8.1, U8.9
  N19: Ch3.5, Ch2.5, J3.pin2, J4.pin2, Ethernet_Jack.pin6
  N20: Ch2.2, Ch1.2, J3.pin1, J4.pin1, Ethernet_Jack.pin7
  N21: Reverb_Switch.L1, J17.pin3, J18.pin3, Ethernet_Jack.pin5
  N22: Reverb_Switch.COM, R7.Pin_0
  N23: Reverb_Switch.L2, Solo_LED1.anode, J8.pin2
  GndOrVolt: J2.pin1, U8.16
  9or-9Switch: J2.pin2, U7.16
  N24: J15.pin2, U7.11
  N25: J15.pin4, U7.9
  N26: D5.anode, D6.anode, R19.Pin_0
  Variable Power Post: Q5.E, U6.Pin_4, R27.Pin_1
  N27: Q5.B, R20.Pin_1, R21.Pin_0
  N28: Q5.C, R22.Pin_1
  PostCouplerPWR: R21.Pin_1, Q6.E, Q7.C, U6.Pin_3
  N29: R23.Pin_1, Q6.C
  N30: Q6.B, R24.Pin_0
  LEDCNTRL: R24.Pin_1, R26.Pin_1, D6.cathode, D3.anode, Ethernet_Jack.pin2
  N31: R25.Pin_1, Q7.E
  N32: R26.Pin_0, Q7.B
  N33: U6.Pin_1, D3.cathode, D4.cathode
  N34: U6.Pin_2, R19.Pin_1
  N35: U7.13, U8.11

custom parts:
  941H-2C-5D: DPDT Relay - 2 Form C
