# Fritzing sketch FootSwitch3 (saved by Fritzing 0.9.3b)
stripboards: 3

parts:
  Solo_LED = LED - 5mm [color="Red (633nm)" package="5 mm [THT]"]
  Solo_Switch = Toggle Switch [package=THT]
  Ch2_LED = LED - 5mm [color="Orange (620nm)" package="5 mm [THT]"]
  Ch1_LED = LED - 5mm [color="Blue (525nm)" package="5 mm [THT]"]
  Amp_Switch = SWITCH-DPDT [package=gpi-152-3013]
  Ethernet_Jack = female pin header, 8 pins [form="♀ (female)"]
  R1 = Resistor [tolerance=±5% resistance=250 package=THT]
  Ethernet_Jack2 = female pin header, 8 pins [form="♀ (female)"]
  U1 = 941H-2C-5D [package=relay-5v]
  U2 = 941H-2C-5D [package=relay-5v]
  U3 = 941H-2C-5D [package=relay-5v]
  AMP_LED = RGB LED (com. cathode, rgb) [package="5 mm [THT]"]
  IC1 = IC, DIP package, 8 pins [chip_label=IC]
  D1 = Rectifier Diode [part_number=1N4001 package="300 mil [THT]"]
  D2 = Rectifier Diode [part_number=1N4001 package="300 mil [THT]"]
  C1 = Electrolytic Capacitor [capacitance=1µF package="100 mil [THT, electrolytic]"]
  C2 = Electrolytic Capacitor [capacitance=1µF package="100 mil [THT, electrolytic]"]
  C3 = Electrolytic Capacitor [capacitance=1µF package="100 mil [THT, electrolytic]"]
  C4 = Electrolytic Capacitor [capacitance=1µF package="100 mil [THT, electrolytic]"]
  Ch3 = SWITCH-DPDT [package=gpi-152-3013]
  Ch2 = SWITCH-DPDT [package=gpi-152-3013]
  Ch1 = SWITCH-DPDT [package=gpi-152-3013]
  R2 = Resistor [tolerance=±5% resistance=270 package=THT]
  Reverb_Switch = Toggle Switch [package=THT]
  Solo_LED1 = LED - 5mm [color="Blue (505nm)" package="5 mm [THT]"]
  J1 = female pin header, 5 pins [form="♀ (female)"]
  J2 = female pin header, 2 pins [form="♀ (female)"]
  Ch3_LED = LED - 5mm [color="Red (633nm)" package="5 mm [THT]"]
  J3 = female pin header, 2 pins [form="♀ (female)"]
  J4 = female pin header, 2 pins [form="♀ (female)"]
  J5 = female pin header, 3 pins [form="♀ (female)"]
  J6 = female pin header, 3 pins [form="♀ (female)"]
  J7 = female pin header, 2 pins [form="♀ (female)"]
  J8 = female pin header, 2 pins [form="♀ (female)"]
  J9 = female pin header, 2 pins [form="♀ (female)"]
  J10 = female pin header, 2 pins [form="♀ (female)"]
  J11 = female pin header, 2 pins [form="♀ (female)"]
  J12 = female pin header, 2 pins [form="♀ (female)"]
  J13 = female pin header, 3 pins [form="♀ (female)"]
  J14 = female pin header, 3 pins [form="♀ (female)"]
  J15 = male pin header, 3 pins [form="♂ (male)"]
  Power_plug1 = Power plug

nets:
  N1: Solo_LED.cathode, Ch2_LED.cathode, Ch1_LED.anode, AMP_LED.common_cathode, R2.Pin_0, Solo_LED1.cathode, Ch3_LED.cathode, J5.pin1, J6.pin1, J7.pin1, J8.pin1, J9.pin2, J10.pin1, J11.pin1, J12.pin1, J13.pin1
  N2: Solo_LED.anode, Solo_Switch.L2, J7.pin2
  N3: Solo_Switch.L1, Ethernet_Jack.pin4
  N4: Solo_Switch.COM, Amp_Switch.2, Amp_Switch.5, Ethernet_Jack.pin1, U1.6, Ch3.3, Ch2.3, Ch2.6, Ch1.3, Reverb_Switch.COM, J9.pin1
  N5: Ch2_LED.anode, U1.11, J11.pin2, J13.pin3
  N6: Ch1_LED.cathode, U1.9, Ch3_LED.anode, J10.pin2, J12.pin2, J13.pin2
  N7: Amp_Switch.1, AMP_LED.red_anode, AMP_LED.green_anode, J5.pin2, J6.pin2
  N8: Amp_Switch.3, AMP_LED.blue_anode, J5.pin3, J6.pin3
  N9: Amp_Switch.6, Ethernet_Jack.pin3
  N10: Ethernet_Jack.pin2, U1.1
  N11: Ethernet_Jack.pin5, Reverb_Switch.L1
  N12: Ethernet_Jack.pin6, Ch3.5, Ch2.5, J3.pin2, J4.pin2
  N13: Ethernet_Jack.pin7, Ch2.2, Ch1.2, J3.pin1, J4.pin1
  N14: Ethernet_Jack.pin8, R2.Pin_1
  N15: R1.Pin_0, U1.8
  N16: R1.Pin_1, U1.16
  N17: Ethernet_Jack2.pin1, U2.9, J15.pin3
  N18: Ethernet_Jack2.pin2, U3.11
  N19: Ethernet_Jack2.pin3, J1.pin1
  N20: Ethernet_Jack2.pin4, J1.pin2
  N21: Ethernet_Jack2.pin5, J1.pin3
  N22: Ethernet_Jack2.pin6, J1.pin4
  N23: Ethernet_Jack2.pin7, J1.pin5
  N24: Ethernet_Jack2.pin8, U2.1, U3.1, J15.pin1
  N25: U1.4, U1.13
  N26: U2.11, J15.pin2
  N27: U2.13, U3.13
  N28: U2.16, J2.pin2
  N29: U3.16, J2.pin1
  9V: IC1.pin1, IC1.pin8, D2.anode, J14.pin3, Power_plug1.VCC
  N30: IC1.pin2, C2.+, C3.-
  GND: IC1.pin3, C1.-, C4.-, J14.pin1, Power_plug1.GND
  N31: IC1.pin4, C2.-
  -9V: IC1.pin5, C4.+, J14.pin2
  18V: D1.cathode, C1.+
  N32: D1.anode, D2.cathode, C3.+
  N33: Reverb_Switch.L2, Solo_LED1.anode, J8.pin2

custom parts:
  941H-2C-5D: DPDT Relay - 2 Form C
