# Fritzing sketch FootSwitch4 (saved by Fritzing 0.9.3b)
stripboards: 4

parts:
  Solo_LED = LED - 5mm [color="Red (633nm)" package="5 mm [THT]"]
  Solo_Switch = Toggle Switch [package=THT]
  Ch2_LED = LED - 5mm [color="Orange (620nm)" package="5 mm [THT]"]
  Ch1_LED = LED - 5mm [color="Blue (525nm)" package="5 mm [THT]"]
  Amp_Switch = SWITCH-DPDT [package=gpi-152-3013]
  Ethernet_Jack = female pin header, 8 pins [form="♀ (female)"]
  Ethernet_Jack2 = female pin header, 8 pins [form="♀ (female)"]
  AMP_LED = RGB LED (com. cathode, rgb) [package="5 mm [THT]"]
  IC1 = IC, DIP package, 8 pins [chip_label=IC]
  D1 = Rectifier Diode [part_number=1N4001 package="300 mil [THT]"]
  D2 = Rectifier Diode [part_number=1N4001 package="300 mil [THT]"]
  C1 = Electrolytic Capacitor [capacitance=1µF package="100 mil [THT, electrolytic]"]
  C2 = Electrolytic Capacitor [capacitance=1µF package="100 mil [THT, electrolytic]"]
  C3 = Electrolytic Capacitor [capacitance=1µF package="100 mil [THT, electrolytic]"]
  Ch3 = SWITCH-DPDT [package=gpi-152-3013]
  Ch2 = SWITCH-DPDT [package=gpi-152-3013]
  Ch1 = SWITCH-DPDT [package=gpi-152-3013]
  Reverb_Switch = Toggle Switch [package=THT]
  Solo_LED1 = LED - 5mm [color="Blue (505nm)" package="5 mm [THT]"]
  J1 = female pin header, 5 pins [form="♀ (female)"]
  J2 = female pin header, 2 pins [form="♀ (female)"]  # not connected
  Ch3_LED = LED - 5mm [color="Red (633nm)" package="5 mm [THT]"]
  J3 = female pin header, 2 pins [form="♀ (female)"]
  J4 = female pin header, 2 pins [form="♀ (female)"]
  J5 = female pin header, 3 pins [form="♀ (female)"]
  J6 = female pin header, 3 pins [form="♀ (female)"]
  J7 = female pin header, 2 pins [form="♀ (female)"]
  J8 = female pin header, 2 pins [form="♀ (female)"]
  J9 = female pin header, 2 pins [form="♀ (female)"]
  J10 = female pin header, 2 pins [form="♀ (female)"]
  J11 = female pin header, 2 pins [form="♀ (female)"]
  J12 = female pin header, 2 pins [form="♀ (female)"]
  J13 = female pin header, 3 pins [form="♀ (female)"]
  R2 = Resistor [tolerance=±5% resistance=220 package=THT]
  R1 = Resistor [tolerance=±5% resistance=220 package=THT]
  R6 = Resistor [tolerance=±5% resistance=220 package=THT]
  R7 = Resistor [tolerance=±10% resistance=220 package=THT]
  R8 = Resistor [tolerance=±5% resistance=220 package=THT]
  J16 = female pin header, 3 pins [form="♀ (female)"]
  J17 = female pin header, 3 pins [form="♀ (female)"]
  J18 = female pin header, 3 pins [form="♀ (female)"]
  C5 = Electrolytic Capacitor [capacitance=100µF package="200 mil [THT, electrolytic]"]
  J19 = female pin header, 2 pins [form="♀ (female)"]
  IC3 = Dual Op-Amp [package=dip08]
  R13 = Resistor [tolerance=±10% resistance=4.7k package=THT]
  R14 = Resistor [tolerance=±5% resistance=4.7k package=THT]
  J14 = female pin header, 5 pins [form="♀ (female)"]
  R15 = Rotary Potentiometer (Large) [maximum_resistance=10kΩ package=THT]
  J15 = male pin header, 5 pins [form="♂ (male)"]
  R12 = Rotary Potentiometer (Large) [maximum_resistance=10kΩ package=THT]
  C6 = Electrolytic Capacitor [capacitance=1µF package="100 mil [THT, electrolytic]"]

nets (from the breadboard view):
  N1: Solo_LED.cathode, Ch2_LED.cathode, Ch1_LED.anode, Ethernet_Jack.pin8, AMP_LED.common_cathode, Solo_LED1.cathode, Ch3_LED.cathode, J5.pin1, J6.pin1, J7.pin1, J8.pin1, J9.pin2, J10.pin1, J11.pin1, J12.pin1, J13.pin1, J16.pin1, C5.-, J19.pin1
  N2: Solo_LED.anode, Solo_Switch.L2, J7.pin2
  N3: Solo_Switch.L1, Ethernet_Jack.pin4, J17.pin2, J18.pin2
  N4: Solo_Switch.COM, R6.Pin_0
  N5: Ch2_LED.anode, J11.pin2, J13.pin3, R2.Pin_1, J16.pin3
  N6: Ch1_LED.cathode, Ch3_LED.anode, J10.pin2, J12.pin2, J13.pin2, R1.Pin_0, J16.pin2
  N7: Amp_Switch.2, R8.Pin_0
  N8: Amp_Switch.5, Ethernet_Jack.pin1, Ch3.3, Ch2.3, Ch2.6, Ch1.3, J9.pin1, R6.Pin_1, R7.Pin_1, R8.Pin_1, J19.pin2
  N9: Amp_Switch.1, AMP_LED.red_anode, AMP_LED.green_anode, J5.pin2, J6.pin2
  N10: Amp_Switch.3, AMP_LED.blue_anode, J5.pin3, J6.pin3
  N11: Amp_Switch.6, Ethernet_Jack.pin3, J17.pin1, J18.pin1
  N12: Ethernet_Jack.pin5, Reverb_Switch.L1, J17.pin3, J18.pin3
  N13: Ethernet_Jack.pin6, Ch3.5, Ch2.5, J3.pin2, J4.pin2
  N14: Ethernet_Jack.pin7, Ch2.2, Ch1.2, J3.pin1, J4.pin1
  N15: Ethernet_Jack2.pin1, J15.pin3
  N16: Ethernet_Jack2.pin2, R15.wiper
  N17: Ethernet_Jack2.pin3, J1.pin1
  N18: Ethernet_Jack2.pin4, J1.pin2
  N19: Ethernet_Jack2.pin5, J1.pin3
  N20: Ethernet_Jack2.pin6, J1.pin4
  N21: Ethernet_Jack2.pin7, J1.pin5
  N22: Ethernet_Jack2.pin8, R15.leg1, J15.pin1
  N23: IC1.pin1, IC1.pin8, D2.anode, IC3.A_V+, R14.Pin_1, J14.pin4
  N24: IC1.pin2, C2.+, C3.-
  N25: IC1.pin3, C1.-, IC3.A_V-, R13.Pin_0, J14.pin1, C6.+
  N26: IC1.pin4, C2.-
  N27: IC1.pin5, J14.pin2, C6.-
  N28: D1.cathode, C1.+, J14.pin5
  N29: D1.anode, D2.cathode, C3.+
  N30: Reverb_Switch.COM, R7.Pin_0
  N31: Reverb_Switch.L2, Solo_LED1.anode, J8.pin2
  N32: IC3.A_OUT, IC3.A_-IN, J14.pin3
  N33: IC3.A_+IN, R12.wiper
  N34: R13.Pin_1, R12.leg1
  N35: R14.Pin_0, R12.leg2
