# Fritzing sketch PowerSwitches (saved by Fritzing 0.9.3b)
stripboards: 2

parts:
  ORANGE_LED = LED - 5mm [color="Red (633nm)" package="5 mm [THT]"]
  PIHRANA_LED = LED - 5mm [color="Red (635nm)" package="5 mm [THT]"]
  R7 = Resistor [tolerance=±10% resistance=390 package=THT]
  U6 = RELAY-2 [package=relay-g5v]  # not connected
  U7 = RELAY-2 [package=relay-g5v]
  R8 = Resistor [tolerance=±10% resistance=180 package=THT]
  J1 = female pin header, 2 pins [form="♀ (female)"]
  J2 = female pin header, 2 pins [form="♀ (female)"]
  LED1 = RGB LED (com. cathode, rgb) [package="5 mm [THT]"]
  J3 = female pin header, 2 pins [form="♀ (female)"]
  J4 = female pin header, 3 pins [form="♀ (female)"]
  J5 = female pin header, 2 pins [form="♀ (female)"]
  J7 = female pin header, 2 pins [form="♀ (female)"]
  J8 = female pin header, 2 pins [form="♀ (female)"]
  J9 = female pin header, 2 pins [form="♀ (female)"]
  J10 = female pin header, 2 pins [form="♀ (female)"]
  J11 = female pin header, 2 pins [form="♀ (female)"]
  R6 = Resistor [tolerance=±5% resistance=820 package=THT]

nets:
  GND: ORANGE_LED.cathode, PIHRANA_LED.cathode, J1.pin2, J2.pin2, LED1.common_cathode, J4.pin2, J8.pin2, J9.pin2, J10.pin2, J11.pin2
  N1: ORANGE_LED.anode, R7.Pin_0, J11.pin1
  N2: PIHRANA_LED.anode, J10.pin1, R6.Pin_0
  N3: R7.Pin_1, J7.pin2, J8.pin1
  N4: U7.2, R8.Pin_0
  9V: U7.5, J3.pin1
  N5: U7.9, LED1.red_anode, J4.pin1
  N6: U7.10, J2.pin1
  12V: R8.Pin_1, J1.pin1, J5.pin2
  N7: LED1.blue_anode, J4.pin3
  N8: J7.pin1, J9.pin1, R6.Pin_1
