# Fritzing sketch SignalManager (saved by Fritzing 0.9.3b)
stripboards: 1

parts:
  U4 = 941H-2C-5D [package=relay-5v]
  Master_Input = Stereo Jack (TRS) 3.5mm [package="PG203J [THT]"]
  ToMesaInput = Stereo Jack (TRS) 3.5mm [package="PG203J [THT]"]
  U5 = LM 358 Dual Op-Amp [package="DIP8 [THT]"]
  U6 = 941H-2C-5D [package=relay-5v]
  ToOrangeInput = Stereo Jack (TRS) 3.5mm [package="PG203J [THT]"]
  ToPihranaInput = Stereo Jack (TRS) 3.5mm [package="PG203J [THT]"]
  OrangeOut = Stereo Jack (TRS) 3.5mm [package="PG203J [THT]"]
  PihranaOut = Stereo Jack (TRS) 3.5mm [package="PG203J [THT]"]
  MesaOut = Stereo Jack (TRS) 3.5mm [package="PG203J [THT]"]
  R1 = Rotary Potentiometer (Large) [maximum_resistance=100kΩ package=THT]
  R2 = Rotary Potentiometer (Large) [maximum_resistance=100kΩ package=THT]
  ToEffects = Stereo Jack (TRS) 3.5mm [package="PG203J [THT]"]
  U7 = LM 358 Dual Op-Amp [package="DIP8 [THT]"]
  R3 = Resistor [tolerance=±5% resistance=220 package=THT]
  R4 = Resistor [tolerance=±5% resistance=220 package=THT]
  Effects_Return = Stereo Jack (TRS) 3.5mm [package="PG203J [THT]"]
  U8 = 941H-2C-5D [package=relay-5v]
  U9 = 941H-2C-5D [package=relay-5v]
  U10 = LM 358 Dual Op-Amp [package="DIP8 [THT]"]
  Effects_Return_2 = Stereo Jack (TRS) 3.5mm [package="PG203J [THT]"]
  R5 = Resistor [tolerance=±5% resistance=220 package=THT]
  R6 = Resistor [tolerance=±5% resistance=220 package=THT]
  J1 = female pin header, 4 pins [form="♀ (female)"]
  J2 = female pin header, 5 pins [form="♀ (female)"]

nets:
  N1: U4.1, J1.pin4
  N2: U4.4, ToMesaInput.Ring
  N3: U4.6, Master_Input.Ring, U5.connector2, U5.connector4
  N4: U4.8, U5.connector5, U5.connector6
  N5: U4.9, R5.Pin_1, R6.Pin_0
  N6: U4.11, MesaOut.Ring, R1.leg1
  N7: U4.13, Effects_Return_2.Ring
  GND: U4.16, Master_Input.Sleeve, ToMesaInput.Sleeve, U6.16, ToOrangeInput.Sleeve, ToPihranaInput.Sleeve, OrangeOut.Sleeve, PihranaOut.Sleeve, MesaOut.Sleeve, R1.leg2, R2.leg1, ToEffects.Sleeve, Effects_Return.Sleeve, U8.16, U9.1, J2.pin1
  N8: U5.connector0, U5.connector1, U6.8
  -9V: U5.connector3, U7.connector3, U10.connector3, J2.pin2
  9V: U5.connector7, U7.connector7, U10.connector7, J2.pin4
  N9: U6.1, J1.pin3
  N10: U6.4, ToOrangeInput.Ring
  N11: U6.6, ToPihranaInput.Ring
  N12: U6.9, R2.leg2
  N13: U6.11, PihranaOut.Ring
  N14: U6.13, OrangeOut.Ring
  N15: R1.wiper, U7.connector4
  N16: R2.wiper, U7.connector2
  N17: ToEffects.Ring, U8.9, U9.8
  N18: U7.connector0, U7.connector1, R3.Pin_1
  N19: U7.connector5, U7.connector6, R4.Pin_1
  N20: R3.Pin_0, U8.13
  N21: R4.Pin_0, U9.4
  N22: Effects_Return.Ring, U10.connector2
  N23: U8.1, J1.pin1
  N24: U8.11, U9.6, U10.connector4
  N25: U9.16, J1.pin2
  N26: U10.connector0, U10.connector1, R5.Pin_0
  N27: U10.connector5, U10.connector6, R6.Pin_1

custom parts:
  941H-2C-5D: DPDT Relay - 2 Form C
