# Fritzing sketch SignalManager2 (saved by Fritzing 0.9.3b)
stripboards: 1

parts:
  U4 = 941H-2C-5D [package=relay-5v]
  U5 = LM 358 Dual Op-Amp [package="DIP8 [THT]"]
  U7 = LM 358 Dual Op-Amp [package="DIP8 [THT]"]
  R4 = Resistor [tolerance=±5% resistance=220 package=THT]
  U8 = 941H-2C-5D [package=relay-5v]
  U9 = 941H-2C-5D [package=relay-5v]
  Effects_Return = Audio Jack (TRS) 3.5mm [package="4Ucon 08780 [THT]"]
  ToMesaInput = Audio Jack (TRS) 3.5mm [package="4Ucon 08780 [THT]"]
  ToOrangeInput = Audio Jack (TRS) 3.5mm [package="4Ucon 08780 [THT]"]
  ToPihranaInput = Audio Jack (TRS) 3.5mm [package="4Ucon 08780 [THT]"]
  Effects_Return_2 = Audio Jack (TRS) 3.5mm [package="4Ucon 08780 [THT]"]
  Master_Input = Audio Jack (TRS) 3.5mm [package="4Ucon 08780 [THT]"]
  OrangeOut = Audio Jack (TRS) 3.5mm [package="4Ucon 08780 [THT]"]
  PihranaOut = Audio Jack (TRS) 3.5mm [package="4Ucon 08780 [THT]"]
  ToEffects = Audio Jack (TRS) 3.5mm [package="4Ucon 08780 [THT]"]
  MesaOut = Audio Jack (TRS) 3.5mm [package="4Ucon 08780 [THT]"]
  J3 = female pin header, 2 pins [form="♀ (female)"]
  R8 = Resistor [tolerance=±5% resistance=100 package=THT]
  R9 = Resistor [tolerance=±5% resistance=100 package=THT]
  R11 = Resistor [tolerance=±5% resistance=1k package=THT]
  R13 = Resistor [tolerance=±5% resistance=47k package=THT]
  J5 = female pin header, 2 pins [form="♀ (female)"]
  J6 = male pin header, 2 pins [form="♂ (male)"]
  J9 = female pin header, 2 pins [form="♀ (female)"]
  J10 = male pin header, 2 pins [form="♂ (male)"]
  J8 = male pin header, 2 pins [form="♂ (male)"]
  J7 = female pin header, 2 pins [form="♀ (female)"]
  J11 = female pin header, 2 pins [form="♀ (female)"]
  J12 = male pin header, 2 pins [form="♂ (male)"]
  J13 = female pin header, 2 pins [form="♀ (female)"]
  J14 = male pin header, 2 pins [form="♂ (male)"]
  J15 = female pin header, 2 pins [form="♀ (female)"]
  J16 = male pin header, 2 pins [form="♂ (male)"]
  J17 = female pin header, 2 pins [form="♀ (female)"]
  J18 = male pin header, 2 pins [form="♂ (male)"]
  J19 = female pin header, 2 pins [form="♀ (female)"]
  J20 = male pin header, 2 pins [form="♂ (male)"]
  J21 = female pin header, 2 pins [form="♀ (female)"]
  J22 = male pin header, 2 pins [form="♂ (male)"]
  J1 = female pin header, 2 pins [form="♀ (female)"]
  R2 = Rotary Potentiometer (Large) [maximum_resistance=10kΩ package=THT]
  Effects_Blend = Rotary Potentiometer (Large) [maximum_resistance=10kΩ package=THT]
  J23 = female pin header, 2 pins [form="♀ (female)"]
  J26 = female pin header, 3 pins [form="♀ (female)"]
  J27 = male pin header, 3 pins [form="♂ (male)"]
  J2 = male pin header, 3 pins [form="♂ (male)"]
  J28 = male pin header, 5 pins [form="♂ (male)"]
  R12 = Resistor [tolerance=±5% resistance=47k package=THT]
  R10 = Resistor [tolerance=±5% resistance=1k package=THT]
  U11 = LM 358 Dual Op-Amp [package="DIP8 [THT]"]
  R3 = Resistor [tolerance=±5% resistance=220 package=THT]
  J4 = male pin header, 2 pins [form="♂ (male)"]
  J30 = male pin header, 3 pins [form="♂ (male)"]
  J29 = female pin header, 3 pins [form="♀ (female)"]
  K1 = Relay [part_number=FRS1B-S package=THT]  # not connected
  K2 = Relay [part_number=FRS1B-S package=THT]  # not connected
  U6 = 941H-2C-5D [package=relay-5v]
  J31 = male pin header, 5 pins [form="♂ (male)"]  # not connected

nets (from the schematic view):
  GND: U4.1, U4.9, U8.1, U9.1, R8.Pin_1, R9.Pin_1, J6.pin2, J10.pin2, J8.pin2, J12.pin2, J14.pin2, J16.pin2, J18.pin2, J20.pin2, J22.pin2, J2.pin1, J28.pin1, J4.pin2, J29.pin2, U6.1
  N1: U4.4, J18.pin1
  N2: U4.6, J14.pin1, U11.connector4
  N3: U4.8, J26.pin2
  N4: U4.11, U5.connector2, J16.pin1
  N5: U4.13, J4.pin1
  N6: U4.16, J23.pin2
  N7: U5.connector0, U5.connector1, U6.8
  -9V: U5.connector3, U7.connector3, J2.pin2, J28.pin2, U11.connector3
  9V: U5.connector7, U7.connector7, J2.pin3, J28.pin4, U11.connector7
  N8: U7.connector0, R10.Pin_0, R3.Pin_1
  N9: U7.connector1, R8.Pin_0, R10.Pin_1
  N10: U7.connector2, R12.Pin_0, J29.pin1
  N11: U7.connector4, R13.Pin_0, J29.pin3
  N12: U7.connector5, R9.Pin_0, R11.Pin_1
  N13: U7.connector6, R4.Pin_1, R11.Pin_0
  N14: R4.Pin_0, U9.13
  N15: U8.9, U9.9, J20.pin1
  N16: U8.11, U9.11, J26.pin1
  N17: U8.13, R3.Pin_0
  N18: U8.16, J1.pin1
  N19: U9.16, J1.pin2
  N20: Effects_Return.Sleeve, J17.pin2
  N21: Effects_Return.Ring, J17.pin1
  N22: ToMesaInput.Sleeve, J3.pin2
  N23: ToMesaInput.Ring, J3.pin1
  N24: ToOrangeInput.Sleeve, J5.pin2
  N25: ToOrangeInput.Ring, J5.pin1
  N26: ToPihranaInput.Sleeve, J7.pin2
  N27: ToPihranaInput.Ring, J7.pin1
  N28: Effects_Return_2.Sleeve, J21.pin2
  N29: Effects_Return_2.Ring, J21.pin1
  N30: Master_Input.Sleeve, J15.pin2
  N31: Master_Input.Ring, J15.pin1
  N32: OrangeOut.Sleeve, J11.pin2
  N33: OrangeOut.Ring, J11.pin1
  N34: PihranaOut.Sleeve, J9.pin2
  N35: PihranaOut.Ring, J9.pin1
  N36: ToEffects.Sleeve, J19.pin2
  N37: ToEffects.Ring, J19.pin1
  N38: MesaOut.Sleeve, J13.pin2
  N39: MesaOut.Ring, J13.pin1
  N40: R13.Pin_1, U11.connector5, U11.connector6
  N41: J6.pin1, U6.4
  N42: J10.pin1, U6.11
  N43: J8.pin1, U6.6
  N44: J12.pin1, U6.13
  N45: J22.pin1, J26.pin3
  N46: R2.leg1, J30.pin3
  N47: R2.wiper, J30.pin2
  N48: R2.leg2, J30.pin1
  N49: Effects_Blend.leg1, J27.pin1
  N50: Effects_Blend.wiper, J27.pin2
  N51: Effects_Blend.leg2, J27.pin3
  N52: J23.pin1, U6.16
  N53: R12.Pin_1, U11.connector0, U11.connector1
  N54: U11.connector2, U6.9

custom parts:
  941H-2C-5D: DPDT Relay - 2 Form C
